# Fritzing sketch ucon19-1 (saved by Fritzing 0.9.3b)
circuit board: 3.91557cm x 5.07214cm
breadboards: 1

parts:
  Servo_Middle = male pin header, 3 pins [form="♂ (male)"]
  Servo_Right = male pin header, 3 pins [form="♂ (male)"]
  JP1 = Header 2 [package=screwterminal-3.5mm-2_lock]
  BT_module = female pin header, 3 pins [form="♀ (female)"]
  Servo_Left = male pin header, 3 pins [form="♂ (male)"]
  Part2 = Arduino Nano (Rev3.0)

nets:
  N1: Servo_Middle.pin1, Part2.D6
  N2: Servo_Middle.pin2, Servo_Right.pin2, BT_module.pin1, Servo_Left.pin2, Part2.5V
  N3: Servo_Middle.pin3, Servo_Right.pin3, JP1.2, BT_module.pin2, Servo_Left.pin3, Part2.GND
  N4: Servo_Right.pin1, Part2.D10
  N5: JP1.1, Part2.VIN
  N6: BT_module.pin3, Part2.D0/RX
  N7: Servo_Left.pin1, Part2.D9

notes:
  Vcc
  Gnd
  signal
  Tx
  M
  R
  L
